# Fritzing sketch Schematic (saved by Fritzing 0.9.3b)
breadboards: 1

parts:
  Raspberry_Pi_1 = Raspberry Pi 3 [part_number=RPI-3-V1.2]
  LCD2 = LCD screen
  LCM1602_IIC2 = LCM1602 IIC [part_number="LCM1602 IIC" chip_label="LCM1602 IIC" package="DIP (Dual Inline) [THT]"]
  S1 = Round Pushbutton
  R1 = Resistor [tolerance=±5% resistance=10k package="0805 [SMD]"]
  Q1 = npn-Powertransistor [package="TO220 [THT]"]
  M1 = DC Motor
  D1 = Diode [package=diode-1n4148]  # not connected
  R2 = Resistor [tolerance=±5% resistance=10k package="0805 [SMD]"]

nets:
  N1: Raspberry_Pi_1.3v3, R1.Pin_0
  N2: Raspberry_Pi_1.GPIO2, LCM1602_IIC2.SDA
  N3: Raspberry_Pi_1.GPIO3, LCM1602_IIC2.SCL
  N4: Raspberry_Pi_1.GIPO26, S1.leg1, R1.Pin_1
  N5: Raspberry_Pi_1.GIPO20, R2.Pin_0
  GND: Raspberry_Pi_1.GND, LCM1602_IIC2.GND, S1.leg0, Q1.emitter
  5V: Raspberry_Pi_1.5V, LCM1602_IIC2.VCC, M1.pin_1
  VSS: LCD2.VSS, LCM1602_IIC2.VSS
  VDD: LCD2.VDD, LCM1602_IIC2.VDD
  N6: LCD2.V0, LCM1602_IIC2.V0
  N7: LCD2.RS, LCM1602_IIC2.RS
  N8: LCD2.R/W, LCM1602_IIC2.RW
  N9: LCD2.E, LCM1602_IIC2.E
  N10: LCD2.DB0, LCM1602_IIC2.D0
  N11: LCD2.DB1, LCM1602_IIC2.D1
  N12: LCD2.DB2, LCM1602_IIC2.D2
  N13: LCD2.DB3, LCM1602_IIC2.D3
  N14: LCD2.DB4, LCM1602_IIC2.D4
  N15: LCD2.DB5, LCM1602_IIC2.D5
  N16: LCD2.DB6, LCM1602_IIC2.D6
  N17: LCD2.DB7, LCM1602_IIC2.D7
  N18: LCD2.LED+, LCM1602_IIC2.A
  N19: LCD2.LED-, LCM1602_IIC2.K
  N20: LCM1602_IIC2.LED_A, LCM1602_IIC2.LED_B
  N21: Q1.base, R2.Pin_1
  N22: Q1.collector, M1.pin_2

notes:
  GPIO26
  GPIO20
  I2C
  3.3v
  5v
  TIP120
  Candy Machine
  Place Pi Camera in Camera Slot
  Serial i2c 20x4 Display

custom parts:
  LCM1602 IIC: I2C-Module to use a 1602 or 2004 LCD on with the wire.h libory Serial LCD Modul
